# Fritzing sketch esp32-pzem-blynk (saved by Fritzing 0.9.5d)

parts:
  A1 = ESP32 devkit 38p expansion board
  A2 = Pzem-004t-pins
  A3 = Current transformer PZCT02
  A4 = 2 channel relay module [package=THT]
  BULB1 = Incandescent light bulb small [package="bulb sm"]
  BULB2 = Incandescent light bulb small [package="bulb sm"]
  J1 = 230V Outlet
  U1 = ESP32-38PinWide [part_number=ESP32-38PinWide]  # not connected

nets:
  N1: A1.Pin_17, A1.Pin_56, A1.Pin_57, A2.5V, A4.Pin_25
  N2: A1.Pin_52, A1.Pin_53, A1.Pin_144, A2.GND#8, A4.Pin_26
  N3: A1.Pin_169, A2.RX
  N4: A1.Pin_170, A2.TX
  N5: A1.Pin_177, A4.Pin_28
  N6: A1.Pin_178, A4.Pin_27
  N7: A2.CT-1, A3.Pin_2
  N8: A2.CT-2, A3.Pin_1
  N9: A2.N, A4.Pin_8, A4.Pin_11, J1.N
  N10: A2.GND#3, BULB1.1, BULB2.1, J1.H
  N11: A4.Pin_7, BULB1.2
  N12: A4.Pin_10, BULB2.2

custom parts:
  ESP32 devkit 38p expansion board: Upgraded ESP32 38P Development ESP32-DevKitC-32 ESP-WROOM-32 Expansion Board.
  Pzem-004t-pins: PZEM-004T 100A AC 80-260V Digital Voltmeter Ammeter Wattmeter Digital Multifunctional Test Pulse Communication TTL Serial Module.
  Current transformer PZCT02: Current transformer PZCT02.
  2 channel relay module: 4 channel Relay Module 5V 12V 24V High and Low Level Trigger Relay Control With Optocoupler Two Way relays DC 5 V 12 V 24 V Volt.
  230V Outlet: 230V power outlet. Note that PCB has been suppressed. (vanepp: changed part name from 120V to 230V replaced moduleId removed terminalIds from breadboard in the fzp file and cleaned up svgs changed part label to J from A and changed label to 230V in schematic.)
  ESP32-38PinWide: Generic 38-Pin ESP32 with wide format (only access to one side of pins on a breadboard) based on Stephen Lilley's HiLetgo ESP-WROOM-32 ESP32 ESP-32S Development Board.
